# Fritzing sketch ModernDevicesRevP (saved by Fritzing 0.9.4)

parts:
  Part1 = Arduino Mega 2560 (Rev3)
  Part2 = Adafruit Ultimate GPS Logger Shield [part_number="Adafruit #1272"]
  Part3 = Adafruit DS3231 [part_number="Adafruit #3013"]
  Pololu_S18V20F12 = DC Power [voltage=12V]
  Part4 = moderndevierevp
  Part5 = moderndevierevp
  Part6 = moderndevierevp
  Part7 = moderndevierevp

nets:
  N1: Part1.A8, Part7.connector23
  N2: Part1.A1, Part6.connector22
  N3: Part1.A2, Part6.connector23
  N4: Part1.A3, Part4.connector22
  N5: Part1.A4, Part4.connector23
  N6: Part1.A5, Part5.connector22
  N7: Part1.A6, Part5.connector23
  N8: Part1.A7, Part7.connector22
  N9: Part1.D21/SCL, Part3.SCL
  N10: Part1.D20/SDA, Part3.SDA
  GND: Part1.GND, Part3.GND, Pololu_S18V20F12.V-, Part4.connector20, Part5.connector20, Part6.connector20, Part7.connector20
  N11: Part1.D13_PWM, Part2.SCK
  N12: Part1.D12_PWM, Part2.MISO
  N13: Part1.D11_PWM, Part2.MOSI
  N14: Part1.D8_PWM, Part2.D8
  5V: Part1.5V, Part3.Vin
  N15: Part1.VIN, Pololu_S18V20F12.V+, Part4.connector21, Part5.connector21, Part6.connector21, Part7.connector21
  N16: Part1.D4_PWM, Part2.D4
  N17: Part1.D7_PWM, Part2.D7

notes:
  SD (4, 11, 12, 13)
  GPS (7, 8)

custom parts:
  Adafruit Ultimate GPS Logger Shield: Brand new and better than ever, we've replaced our Adafruit GPS shield kit with this assembled shield that comes with an Ultimate GPS module. This GPS shield works great with either UNO or Leonardo Arduinos and is designed to log data to an SD card. Or you can leave the SD card out and use the GPS for a geocaching project, or maybe a music player that changes tunes depending on where you are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
  Adafruit DS3231: The datasheet for the DS3231 explains that this part is an "Extremely Accurate I²C-Integrated RTC/TCXO/Crystal". And, hey, it does exactly what it says on the tin! This Real Time Clock (RTC) is the most precise you can get in a small, low power package. Most RTCs use an external 32kHz timing crystal that is used to keep time with low current draw. And that's all well and good, but those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
